// Logisim project ALU_Control.circ as structural Verilog: 1 circuit, main circuit main
module main (
  input  ALUOp1,
  input  ALUOp0,
  input  Func5,
  input  Func4,
  input  Func3,
  input  Func2,
  input  Func1,
  input  Func0,
  output ALUControl2,
  output ALUControl1,
  output ALUControl0
);

  wire and_1_out, and_2_out, and_3_out, not_1_out, not_2_out;

  and and_1 (and_1_out, ALUOp1, Func1);
  not not_1 (not_1_out, ALUOp1);
  not not_2 (not_2_out, Func2);
  and and_2 (and_2_out, ALUOp1, Func0);
  and and_3 (and_3_out, ALUOp1, Func3);
  or or_1 (ALUControl2, ALUOp0, and_1_out);
  or or_2 (ALUControl1, not_1_out, not_2_out);
  or or_3 (ALUControl0, and_2_out, and_3_out);
endmodule
