// Logisim project ALU_controll1.circ as structural Verilog
module main3_alu (
  input  ALUOp1,
  input  ALUOp0,
  input  Fun5,
  input  Fun4,
  input  Fun3,
  input  Func2,
  input  Func1,
  input  Func0,
  output ALUControl2,
  output ALUControl1,
  output ALUControl0
);

  wire and_1_out, and_2_out, and_3_out, not_1_out, not_2_out;

  and and_1 (and_1_out, ALUOp1, Func1);
  not not_1 (not_1_out, ALUOp1);
  or or_1 (ALUControl1, not_1_out, not_2_out);
  not not_2 (not_2_out, Func2);
  and and_2 (and_2_out, ALUOp1, Func0);
  and and_3 (and_3_out, ALUOp1, Fun3);
  or or_2 (ALUControl2, ALUOp0, and_1_out);
  or or_3 (ALUControl0, and_2_out, and_3_out);
endmodule
