// Logisim project DATAMEM.circ as structural Verilog: 1 circuit, main circuit main
module main (
  input  [31:0] RD,
  input  [8:0] A,
  input  CLK,
  input  MemWrite,
  input  [31:0] WD,
  input  [31:0] \output 
);

  wire and_1_out, nor_1_out, not_1_out;
  wire [31:0] ram_1_data, register_1_q;

  nor nor_1 (nor_1_out, A[8], A[7], A[6], A[5], A[4], A[3], A[2], A[1], A[0]);
  RAM #(.addrWidth(7), .dataWidth(32)) ram_1 (
    .addr(A[8:2]), .data(ram_1_data), .clk(CLK), .ld(not_1_out));  // open: sel, clr
  not not_1 (not_1_out, MemWrite);
  and and_1 (and_1_out, MemWrite, nor_1_out);
  assign ram_1_data = MemWrite ? WD : 32'bz;  // Controlled_Buffer controlled_buffer_1
  Register #(.width(32)) register_1 (.D(WD), .en(and_1_out), .Q(register_1_q), .clk(CLK));  // open: clr

  // Notes on the sheet:
  //   Id: 1 -> Memory Value -> RD
endmodule
