// Logisim project REGFİLE.circ as structural Verilog: 1 circuit, main circuit main
module main (
  input  [4:0] A1,
  input  [4:0] A2,
  input  [31:0] RD1,
  input  [4:0] A3,
  input  [31:0] RD2,
  input  [31:0] WD3,
  input  in_7,
  input  in_8
);

  wire demultiplexer_1_out0, demultiplexer_1_out1;
  wire [31:0] demultiplexer_2_out0, demultiplexer_2_out1, multiplexer_1_out, multiplexer_2_out, undriven,
       undriven_2, undriven_3, undriven_4;

  Demultiplexer demultiplexer_1 (
    .out0(demultiplexer_1_out0), .out1(demultiplexer_1_out1), .in(in_8), .sel(A3[4]));  // open: en
  Demultiplexer #(.width(32)) demultiplexer_2 (
    .out0(demultiplexer_2_out0), .out1(demultiplexer_2_out1), .in(WD3), .sel(A3[4]));  // open: en
  \REGFİLE16_main  main_1 (
    .A1(A1[3:0]), .A2(A2[3:0]), .CLK(in_7), .WE(demultiplexer_1_out0), .RD1(undriven), .A3(A3[3:0]),
    .WD3(demultiplexer_2_out0), .RD2(undriven_2));
  \REGFİLE16_main  main_2 (
    .A1(A1[3:0]), .A2(A2[3:0]), .CLK(in_7), .WE(demultiplexer_1_out1), .RD1(undriven_3), .A3(A3[3:0]),
    .WD3(demultiplexer_2_out1), .RD2(undriven_4));
  Multiplexer #(.width(32)) multiplexer_1 (
    .in0(undriven), .in1(undriven_3), .out(multiplexer_1_out), .sel(A1[4]));  // open: en
  Multiplexer #(.width(32)) multiplexer_2 (
    .in0(undriven_2), .in1(undriven_4), .out(multiplexer_2_out), .sel(A2[4]));  // open: en
endmodule
