// Logisim project REGFİLE16.circ as structural Verilog: 1 circuit, main circuit main
module main (
  input  [3:0] A1,
  input  [3:0] A2,
  input  CLK,
  input  WE,
  input  [31:0] RD1,
  input  [3:0] A3,
  input  [31:0] WD3,
  input  [31:0] RD2
);

  wire demultiplexer_1_out0, demultiplexer_1_out1, demultiplexer_1_out2, demultiplexer_1_out3;
  wire [31:0] demultiplexer_2_out0, demultiplexer_2_out1, demultiplexer_2_out2, demultiplexer_2_out3,
       main_1_rd1, main_1_rd2, main_2_rd1, main_2_rd2, main_3_rd1, main_3_rd2, main_4_rd2, multiplexer_1_out,
       multiplexer_2_out;

  Demultiplexer #(.select(2)) demultiplexer_1 (
    .out0(demultiplexer_1_out0), .out1(demultiplexer_1_out1), .out2(demultiplexer_1_out2),
    .out3(demultiplexer_1_out3), .in(WE), .sel(A3[3:2]));  // open: en
  Demultiplexer #(.select(2), .width(32)) demultiplexer_2 (
    .out0(demultiplexer_2_out0), .out1(demultiplexer_2_out1), .out2(demultiplexer_2_out2),
    .out3(demultiplexer_2_out3), .in(WD3), .sel(A3[3:2]));  // open: en
  \REGFİLE1_main  main_1 (
    .A1(A1[1:0]), .A2(A3[1:0]), .WD3(demultiplexer_2_out0), .A3(A2[1:0]), .WE(demultiplexer_1_out0),
    .CLK(CLK), .RD1(main_1_rd1), .RD2(main_1_rd2));
  \REGFİLE1_main  main_2 (
    .A1(A1[1:0]), .A2(A3[1:0]), .WD3(demultiplexer_2_out1), .A3(A2[1:0]), .WE(demultiplexer_1_out1),
    .CLK(CLK), .RD1(main_2_rd1), .RD2(main_2_rd2));
  \REGFİLE1_main  main_3 (
    .A1(A1[1:0]), .A2(A3[1:0]), .WD3(demultiplexer_2_out2), .A3(A2[1:0]), .WE(demultiplexer_1_out2),
    .CLK(CLK), .RD1(main_3_rd1), .RD2(main_3_rd2));
  \REGFİLE1_main  main_4 (
    .A1(A1[1:0]), .A2(A3[1:0]), .WD3(demultiplexer_2_out3), .A3(A2[1:0]), .WE(demultiplexer_1_out3),
    .CLK(CLK), .RD1(main_1_rd2), .RD2(main_4_rd2));
  Multiplexer #(.select(2), .width(32)) multiplexer_1 (
    .in0(main_1_rd1), .in1(main_2_rd1), .in2(main_3_rd1), .in3(main_1_rd2), .out(multiplexer_1_out),
    .sel(A1[3:2]));  // open: en
  Multiplexer #(.select(2), .width(32)) multiplexer_2 (
    .in0(main_1_rd2), .in1(main_2_rd2), .in2(main_3_rd2), .in3(main_4_rd2), .out(multiplexer_2_out),
    .sel(A2[3:2]));  // open: en
endmodule
