// Logisim project main_control.circ as structural Verilog: 1 circuit, main circuit main
module main (
  input  [5:0] Opcode,
  input  [5:0] Func,
  output RegWrite,
  output RegDst,
  output ALUSrc,
  output Branch,
  output MemWrite,
  output MemtoReg,
  output Jump,
  output [2:0] ALUControl
);

  wire main_1_aluop0, main_1_out_12;

  main_decoder_main main_1 (
    .op5(Opcode[5]), .op4(Opcode[4]), .op3(Opcode[3]), .op2(Opcode[2]), .op1(Opcode[1]), .op0(Opcode[0]),
    .RegWrite(RegWrite), .RegDst(RegDst), .AluSrc(ALUSrc), .Branch(Branch), .MemWrite(MemWrite),
    .ALUOp1(MemtoReg), .out_12(main_1_out_12), .ALUOp0(main_1_aluop0), .JUMP(Jump));
  ALU_Control_main main_2 (
    .ALUOp1(main_1_out_12), .ALUOp0(main_1_aluop0), .Func5(Func[5]), .Func4(Func[4]), .Func3(Func[3]),
    .Func2(Func[2]), .Func1(Func[1]), .Func0(Func[0]), .ALUControl2(ALUControl[2]),
    .ALUControl1(ALUControl[1]), .ALUControl0(ALUControl[0]));
endmodule
