// Logisim project maincontrol1.circ as structural Verilog: 1 circuit, main circuit main
module main (
  input  [5:0] Opcode,
  input  [2:0] ALUControl,
  input  [5:0] Func,
  output RegWrite,
  output RegDst,
  output ALUSrc,
  output Branch,
  output MemWrite,
  output MemtoReg,
  output Jump
);

  wire main1_1_aluop0, main1_1_aluop1;

  main1 main1_1 (
    .op5(Opcode[5]), .op4(Opcode[4]), .op3(Opcode[3]), .op2(Opcode[2]), .op1(Opcode[1]), .op0(Opcode[0]),
    .RegWrite(RegWrite), .RegDst(RegDst), .ALUSrc(ALUSrc), .Branch(Branch), .MemWrtie(MemWrite),
    .MemtoReg(MemtoReg), .ALUOp1(main1_1_aluop1), .ALUOp0(main1_1_aluop0), .Jump(Jump));
  main3_alu main3_alu_1 (
    .ALUOp1(main1_1_aluop1), .ALUOp0(main1_1_aluop0), .Fun5(Func[5]), .Fun4(Func[4]), .Fun3(Func[3]),
    .Func2(Func[2]), .Func1(Func[1]), .Func0(Func[0]), .ALUControl2(ALUControl[2]),
    .ALUControl1(ALUControl[1]), .ALUControl0(ALUControl[0]));
endmodule
