// Logisim project mips_datapath.circ as structural Verilog: 1 circuit, main circuit main
module main (
  input  MemtoReg,
  input  RegDst,
  input  MemWrite,
  input  WE,
  input  [2:0] ALU_Ctrl,
  input  ALUSrc,
  input  Branch
);

  wire and_1_out, button_1_out, clock_1_out, main_2_p5;
  wire [4:0] multiplexer_2_out;
  wire [7:0] adder_1_out, multiplexer_1_out, register_1_q;
  wire [8:0] undriven_2;
  wire [31:0] adder_2_out, bit_extender_1_out, bit_extender_2_out, main_2_p1, main_2_p4, multiplexer_3_out,
       multiplexer_4_out, rom_1_data, shifter_1_out, undriven, undriven_3;

  Multiplexer #(.width(8)) multiplexer_1 (
    .in0(adder_1_out), .in1(adder_2_out[7:0]), .out(multiplexer_1_out), .sel(and_1_out));  // open: en
  Clock clock_1 (.out(clock_1_out));
  Button button_1 (.out(button_1_out));
  Register register_1 (.D(multiplexer_1_out), .Q(register_1_q), .clk(clock_1_out), .clr(button_1_out));  // open: en
  Adder adder_1 (.a(register_1_q), .b(8'h4), .out(adder_1_out));  // open: cin, cout
  ROM #(.addrWidth(6), .dataWidth(32)) rom_1 (.addr(register_1_q[7:2]), .data(rom_1_data));  // open: sel
  // Probe on rom_1_data[20:16]
  assign bit_extender_1_out = {{24{1'b0}}, adder_1_out};  // Bit_Extender bit_extender_1
  // Probe on rom_1_data[31:26]
  Multiplexer #(.width(5)) multiplexer_2 (
    .in0(rom_1_data[20:16]), .in1(rom_1_data[15:11]), .out(multiplexer_2_out), .sel(RegDst));  // open: en
  assign bit_extender_2_out = {{16{rom_1_data[15]}}, rom_1_data[15:0]};  // Bit_Extender bit_extender_2
  \REGFİLE_main  main_1 (
    .A1(rom_1_data[25:21]), .A2(rom_1_data[20:16]), .RD1(main_2_p1), .A3(multiplexer_2_out), .RD2(undriven),
    .WD3(multiplexer_4_out), .in_7(clock_1_out), .in_8(WE));
  Shifter #(.width(32)) shifter_1 (.in(bit_extender_2_out), .\dist (5'b00010), .out(shifter_1_out));
  Multiplexer #(.width(32)) multiplexer_3 (
    .in0(undriven), .in1(bit_extender_2_out), .out(multiplexer_3_out), .sel(ALUSrc));  // open: en
  Adder #(.width(32)) adder_2 (.a(shifter_1_out), .b(bit_extender_1_out), .out(adder_2_out));  // open: cin, cout
  // ALU32_main main_2: pin names not known; wires that end beside it: main_2_p1, multiplexer_3_out, ALU_Ctrl, main_2_p4, main_2_p5
  and and_1 (and_1_out, main_2_p5, Branch);
  Multiplexer #(.width(32)) multiplexer_4 (
    .in0(main_2_p4), .in1(undriven_3), .out(multiplexer_4_out), .sel(MemtoReg));  // open: en
  DATAMEM_main main_3 (
    .RD(undriven_3), .A(undriven_2), .CLK(clock_1_out), .MemWrite(MemWrite), .WD(undriven));  // open: output

  // Notes on the sheet:
  //   lw $t2 , 32($t0)
  //   014b4820 -> add $t1 ,$t2 , $t3
  //   112a0004 -> beq $t1 ,$t2 , 0x4
  //   contents of rom_1 (hex, n*v repeats v):
  //   8c0a0020 8c0a0020 14b4280 aad49004 112a0004
  //   F=010 ->ADD
endmodule
