// Logisim project mıps_processor.circ as structural Verilog: 1 circuit, main circuit main
module main (
  input  [31:0] RD,
  input  [8:0] A,
  input  CLK,
  input  MemWrite,
  input  [31:0] WD
);

  wire not_1_out;
  wire [31:0] ram_1_data;

  not not_1 (not_1_out, MemWrite);
  RAM #(.addrWidth(7), .dataWidth(32)) ram_1 (
    .addr(A[8:2]), .data(ram_1_data), .clk(CLK), .ld(not_1_out));  // open: sel, clr
  assign ram_1_data = MemWrite ? WD : 32'bz;  // Controlled_Buffer controlled_buffer_1

  // Notes on the sheet:
  //   Id: 1 -> Memory Value -> RD
endmodule
