// Logisim project ÖDEV.circ as structural Verilog: 1 circuit, main circuit main
module main (
  input  JUMP
);

  wire AluSrc, and_1_out, Branch, button_1_out, clock_1_out, Jump_t, main_1_zero, MemtoReg, MemWrite, RegDst,
       RegWrite;
  wire [2:0] ALUControl;
  wire [4:0] multiplexer_3_out;
  wire [5:0] Func, Opcode;
  wire [7:0] adder_1_out, adder_2_out, multiplexer_1_out, multiplexer_2_out, register_1_q, shifter_1_out;
  wire [8:0] main_1_y;
  wire [19:0] shifter_1_out_2;
  wire [22:0] main_1_y_2;
  wire [25:6] rom_1_data;
  wire [27:0] bit_extender_2_out;
  wire [31:0] bit_extender_1_out, bit_extender_3_out, multiplexer_4_out, multiplexer_5_out, shifter_2_out,
       undriven, undriven_2, undriven_3, undriven_4;
  wire [31:8] adder_2_out_2;

  Multiplexer #(.width(8)) multiplexer_1 (
    .in0(adder_1_out), .in1(adder_2_out), .out(multiplexer_1_out), .sel(and_1_out));  // open: en
  Clock clock_1 (.out(clock_1_out));
  Multiplexer #(.width(8)) multiplexer_2 (
    .in0(multiplexer_1_out), .in1(shifter_1_out), .out(multiplexer_2_out), .sel(JUMP));  // open: en
  Button button_1 (.out(button_1_out));
  Register register_1 (.D(multiplexer_2_out), .Q(register_1_q), .clk(clock_1_out), .clr(button_1_out));  // open: en
  Adder adder_1 (.a(register_1_q), .b(8'h4), .out(adder_1_out));  // open: cin, cout
  assign bit_extender_1_out = {{24{adder_1_out[7]}}, adder_1_out};  // Bit_Extender bit_extender_1
  ROM #(.addrWidth(6), .dataWidth(32)) rom_1 (
    .addr(register_1_q[7:2]), .data({Opcode, rom_1_data, Func}));  // open: sel
  Multiplexer #(.width(5)) multiplexer_3 (
    .in0(rom_1_data[20:16]), .in1(rom_1_data[15:11]), .out(multiplexer_3_out), .sel(RegDst));  // open: en
  // Probe on rom_1_data[20:16]
  assign bit_extender_2_out = {{2{rom_1_data[25]}}, {rom_1_data, Func}};  // Bit_Extender bit_extender_2
  assign bit_extender_3_out = {{16{rom_1_data[15]}}, {rom_1_data[15:6], Func}};  // Bit_Extender bit_extender_3
  Shifter #(.width(28)) shifter_1 (.in(bit_extender_2_out), .\dist (5'b00011), .out({shifter_1_out_2, shifter_1_out}));
  \REGFİLE_main  WE (
    .A1(rom_1_data[25:21]), .A2(rom_1_data[20:16]), .RD1(undriven), .A3(multiplexer_3_out), .RD2(undriven_2),
    .WD3(multiplexer_5_out), .in_7(clock_1_out), .in_8(RegWrite));
  Shifter #(.width(32)) shifter_2 (.in(bit_extender_3_out), .\dist (5'b00010), .out(shifter_2_out));
  Multiplexer #(.width(32)) multiplexer_4 (
    .in0(undriven_2), .in1(bit_extender_3_out), .out(multiplexer_4_out), .sel(AluSrc));  // open: en
  Adder #(.width(32)) adder_2 (
    .a(shifter_2_out), .b(bit_extender_1_out), .out({adder_2_out_2, adder_2_out}));  // open: cin, cout
  ALU32_main main_1 (
    .A(undriven), .B(multiplexer_4_out), .F(ALUControl), .Y({main_1_y_2, main_1_y}), .Zero(main_1_zero));
  and and_1 (and_1_out, Branch, main_1_zero);
  DATAMEM_main main_2 (
    .RD(undriven_4), .A(main_1_y), .CLK(clock_1_out), .MemWrite(MemWrite), .WD(undriven_2),
    .\output (undriven_3));
  maincontrol1_main main_3 (
    .Opcode(Opcode), .Func(Func), .RegWrite(RegWrite), .RegDst(RegDst), .ALUSrc(AluSrc), .Branch(Branch),
    .MemWrite(MemWrite), .MemtoReg(MemtoReg), .Jump(Jump_t), .ALUControl(ALUControl));
  Multiplexer #(.width(32)) multiplexer_5 (
    .in0({main_1_y_2, main_1_y}), .in1(undriven_4), .out(multiplexer_5_out), .sel(MemtoReg));  // open: en
  _7_Segment_Display u_7_segment_display_1 (
    .g(undriven_3[6]), .f(undriven_3[7]), .a(undriven_3[1]), .b(undriven_3[0]), .e(undriven_3[5]),
    .d(undriven_3[4]), .c(undriven_3[3]), .dp(undriven_3[2]));
  _7_Segment_Display u_7_segment_display_2 (
    .g(undriven_3[14]), .f(undriven_3[15]), .a(undriven_3[9]), .b(undriven_3[8]), .e(undriven_3[13]),
    .d(undriven_3[12]), .c(undriven_3[11]), .dp(undriven_3[10]));

  // Notes on the sheet:
  //   lw $t2 , 32($t0)
  //   014b4820 -> add $t1 ,$t2 , $t3
  //   112a0004 -> beq $t1 ,$t2 , 0x4
  //   contents of rom_1 (hex, n*v repeats v):
  //   20010abb 20ac0100 2001730a ac010000 2001730a ac010000 2001ca6b ac010000 2001d9ca ac010000 2001f9d9
  //   ac010000 20010bf9 ac010000 2001fb0b ac010000 2001dbfb ac010000 2001bbdb ac010000 8000000
  //   F=010 ->ADD
  //   MEMORY MAPPED IO
  //   MEMORY MAPPED IO
endmodule
