// Logisim project İNSTRUCTON.circ as structural Verilog: 1 circuit, main circuit main
module main (
  input  clear,
  output [31:0] out_2,
  output [31:0] out_3
);

  wire clock_1_out;
  wire [31:0] register_1_q;

  Register #(.width(32)) register_1 (.D(out_2), .Q(register_1_q), .clk(clock_1_out), .clr(clear));  // open: en
  Clock clock_1 (.out(clock_1_out));
  Adder #(.width(32)) adder_1 (.a(register_1_q), .b(32'h4), .out(out_2));  // open: cin, cout
  ROM #(.dataWidth(32)) rom_1 (.addr(register_1_q[7:0]), .data(out_3));  // open: sel

  // Notes on the sheet:
  //   instruction fetch
  //   instruction memory
  //   PC
  //   instruction
endmodule
